// Digital circuit CORE.dig as structural Verilog
module CORE (
  input  clk,
  input  RST,
  input  CLR,
  input  in_4,
  input  [11:0] MIPCBI,
  input  [15:0] PCBI,
  input  MIPCBE,
  input  PCBE
);

  wire ALUD_CO, ALUDH_OE, ALUDL_OE, ALUS_OE, and_3_out, and_4_out, and_5_out, ASSERT_p5, BR_Q, button_1_out,
       CLK_t, CLKR, comparator_1_eq, comparator_1_gt, comparator_1_lt, comparator_2_eq, comparator_3_eq,
       DC_JUMP, EXT_p5, IMMED_OE, IRQ_OE, not_1_out, or_1_out, RAM_OE, RAM_WE, RF_HWE, RF_LWE, RF_SFR,
       RFSRCR_WE, ROM_OE, SFR_OE, SR_WE, WR_WE, XRAM_OE;
  wire [2:0] BR_SRC, BUS_SRC, JUMP_TYPE;
  wire [3:0] ALUSD_FUNC, multiplexer_2_out, RF_SRC;
  wire [5:4] multiplexer_2_out_2;
  wire [6:0] and_2_out;
  wire [7:0] DBUS, IMMED, RADDR, RF_Q, WR_q;
  wire [7:4] RFSRCR_q;
  wire [11:0] ADDRESS, MIPC;
  wire [15:0] pce_1_q;
  wire [47:44] DECODER_2_d;

  DCOUTER #(.generic("Bits := 12;")) dcouter_1 (
    .CLK(CLK_t), .CLR(CLR), .CNT(1'b1), .LE(DC_JUMP), .D(ADDRESS), .Q(MIPC));
  Comparator #(.Bits(8)) comparator_1 (
    .a(RF_Q), .b(IMMED), .gt(comparator_1_gt), .eq(comparator_1_eq), .lt(comparator_1_lt));
  Decoder #(.Selector_Bits(3)) decoder_1 (
    .sel(BUS_SRC), .out_0(ALUS_OE), .out_1(ALUDL_OE), .out_2(ALUDH_OE), .out_3(IMMED_OE), .out_4(RAM_OE),
    .out_5(XRAM_OE), .out_6(ROM_OE), .out_7(IRQ_OE));
  Multiplexer #(.Selector_Bits(3)) multiplexer_1 (
    .sel(JUMP_TYPE), .in_0(1'b0), .in_1(1'b1), .in_2(comparator_1_gt), .in_3(comparator_1_eq),
    .in_4(comparator_1_lt), .in_5(BR_Q), .in_6(RST), .in_7(1'b0), .out(DC_JUMP));
  PCE pce_1 (.CLK(CLK_t), .D(DBUS), .RS(RF_SRC), .LWE(RF_LWE), .HWE(RF_HWE), .Q(pce_1_q));
  ROM #(.AddrBits(12), .Bits(48)) DECODER_2 (
    .A(MIPC), .sel(1'b1),
    .D({DECODER_2_d, IMMED, ADDRESS, JUMP_TYPE, ALUSD_FUNC, RAM_WE, RFSRCR_WE, BR_SRC, SR_WE, WR_WE, BUS_SRC, RF_SFR, RF_HWE, RF_LWE, RF_SRC}));
  Register #(.Bits(8)) RFSRCR (.D(DBUS), .C(CLK_t), .en(RFSRCR_WE), .Q({RFSRCR_q, and_2_out[3:0]}));
  and and_1 (and_2_out[5], RFSRCR_q[4], RAM_WE);
  and and_2 (and_2_out[6], RFSRCR_q[4], RAM_OE);
  Comparator #(.Bits(12)) comparator_2 (.a(MIPCBI), .b(MIPC), .eq(comparator_2_eq));  // open: gt, lt
  Comparator #(.Bits(16)) comparator_3 (.a(PCBI), .b(pce_1_q), .eq(comparator_3_eq));  // open: gt, lt
  and and_3 (and_3_out, comparator_2_eq, MIPCBE);
  and and_4 (and_4_out, comparator_3_eq, PCBE);
  Multiplexer #(.Bits(7)) multiplexer_2 (
    .sel(RF_SFR), .in_0({1'b0, RF_HWE, RF_LWE, RF_SRC}),
    .in_1({and_2_out[6:5], and_2_out[5], and_2_out[3:0]}),
    .out({SFR_OE, multiplexer_2_out_2, multiplexer_2_out}));
  // Probe on MIPC
  // Probe on RF_SRC
  // Probe on RF_LWE
  // Probe on RF_HWE
  // Probe on RF_SFR
  // Probe on BUS_SRC
  // Probe on WR_WE
  // Probe on SR_WE
  // Probe on BR_SRC
  // Probe on RFSRCR_WE
  // Probe on RAM_WE
  // Probe on ALUSD_FUNC
  // Probe on JUMP_TYPE
  // Probe on ADDRESS
  // Probe on IMMED
  // ASSERT ASSERT: pin names not known; wires that end beside it: CLK_t, DBUS, RADDR, RAM_WE, ASSERT_p5, CLK_t
  Button button_1 (.out(button_1_out));
  // reg_file RF: pin names not known; wires that end beside it: CLK_t, multiplexer_2_out, DBUS, multiplexer_2_out_2[4], multiplexer_2_out_2[5], RF_Q
  BR BR (.CLK(CLK_t), .CLR(CLR), .S(BR_SRC), .ALUDF(ALUD_CO), .ALUSF(ALUD_CO), .A0(RF_Q[0]), .A7(RF_Q[7]), .Q(BR_Q));
  or or_1 (or_1_out, ASSERT_p5, and_3_out, and_4_out);
  // SwitchDT switchdt_1: pin names not known; wires that end beside it: clk, button_1_out, CLKR
  // Probe on RF_Q
  STALL STALL (.C(CLKR), .AC(or_1_out), .S(in_4), .OAC(CLK_t));  // open: G, nCLR, O
  reg__sync_clear #(.generic("Bits := 8;")) WR (.D(DBUS), .CLK(CLK_t), .CLR(CLR), .LE(WR_WE), .Q(WR_q));
  reg__sync_clear #(.generic("Bits := 8;")) SR (.D(DBUS), .CLK(CLK_t), .CLR(CLR), .LE(SR_WE), .Q(RADDR));
  not not_1 (not_1_out, CLK_t);
  PullDown #(.Bits(8)) pulldown_1 (.out(DBUS));
  assign DBUS = SFR_OE ? RF_Q : 8'bz;  // Driver driver_1
  // Probe on WR_q
  // Probe on RADDR
  and and_5 (and_5_out, RAM_WE, CLK_t, not_1_out);
  // Probe on DBUS
  ALU ALU (
    .A(RF_Q), .B(WR_q), .S(ALUSD_FUNC), .CI(BR_Q), .nSOE(ALUS_OE), .nDLOE(ALUDL_OE), .nDHOE(ALUDH_OE),
    .O(DBUS), .CO(ALUD_CO));
  // Probe on {RADDR, WR_q}
  ROM #(.AddrBits(16), .Bits(8)) ROM (.A({RADDR, WR_q}), .sel(ROM_OE), .D(DBUS));
  RAMSinglePortSel #(.AddrBits(7), .isProgramMemory("true"), .Bits(8)) RAM (
    .A(RADDR[6:0]), .CS(~RADDR[7]), .WE(and_5_out), .OE(RAM_OE), .D(DBUS));
  // EXTCTL EXT: pin names not known; wires that end beside it: RAM_WE, RADDR, DBUS, CLK_t, EXT_p5
  // Probe on EXT_p5
  assign DBUS = IMMED_OE ? IMMED : 8'bz;  // Driver driver_2

  // Other names for the same wires on the sheet: GO = in_4

  // Notes on the sheet:
  //   clk: Hz: 2147483647
  //   contents of DECODER_2 (hex, n*v repeats v):
  //   12fc80488,80889,33a,85106,1c3135,1e54b8,1e08b9,8008c80000a,c004480000a,e002580000a,
  //   f001680000a,f801080040a,a00bc,80485,1a088c,236,f401380000a,f601280000a,f501380000a,
  //   f201580000a,f301580000a,f101680000a,e801e80000a,ec01b80000a,ee01a80000a,ef01a80000a,
  //   ed01b80000a,ea01d80000a,eb01d80000a,e901e80000a,e402280000a,e602180000a,e702180000a,
  //   e502280000a,e202480000a,e302480000a,e102580000a,d003580000a,d802e80000a,dc02b80000a,
  //   de02a80000a,df02a80000a,dd02b80000a,da02d80000a,db02d80000a,d902e80000a,d403280000a,
  //   d603180000a,d703180000a,d503280000a,d203480000a,d303480000a,d103580000a,c803d80000a,
  //   cc03a80000a,ce03980000a,cf03980000a,cd03a80000a,ca03c80000a,cb03c80000a,c903d80000a,
  //   c404180000a,c604080000a,c704080000a,c504180000a,c204380000a,c304380000a,c104480000a,
  //   a006780000a,b005580000a,b804e80000a,bc04b80000a,be04a80000a,bf04a80000a,bd04b80000a,
  //   ba04d80000a,bb04d80000a,b904e80000a,b405280000a,b605180000a,b705180000a,b505280000a,
  //   b205480000a,b305480000a,b105580000a,a805d80000a,ac05a80000a,ae05980000a,af05980000a,
  //   ad05a80000a,aa05c80000a,ab05c80000a,a905d80000a,a406180000a,a606080000a,a706080000a,
  //   a506180000a,a206680000a,a306680000a,3580,450b1,1172400b2,a106780000a,9006f80000a,
  //   9806980000a,9406c80000a,9606b80000a,9506c80000a,9206e80000a,9306e80000a,9106f80000a,
  //   8807780000a,8c07480000a,8e07380000a,8f07380000a,8d07480000a,8a07680000a,8b07680000a,
  //   8907780000a,8408980000a,8607a80000a,8707a80000a,8508980000a,fd000000980,10000,b3c,
  //   6800c,640,a30bd,1e54b8,1e08b9,8048d,b3c,6800c,b30c0,1e54b8,1173e08b9,8208b80000a,
  //   8308b80000a,8108c80000a,400d580000a,600b680000a,700a780000a,7809780000a,7c09480000a,
  //   7e09380000a,7f09380000a,7d09480000a,7a09680000a,7b09680000a,7909780000a,740a480000a,
  //   7609a80000a,7709a80000a,750a480000a,333c,1e54b8,1e08b9,700,6800c,8088c,b30c0,1e50b8,
  //   1173e00b9,720a680000a,730a680000a,710a780000a,680af80000a,6c0ac80000a,6e0ab80000a,
  //   6f0ab80000a,6d0ac80000a,6a0ae80000a,6b0ae80000a,690af80000a,640b380000a,660b280000a,
  //   670b280000a,650b380000a,620b580000a,630b580000a,610b680000a,500c680000a,580bf80000a,
  //   5c0bc80000a,5e0bb80000a,5f0bb80000a,5d0bc80000a,5a0be80000a,5b0be80000a,590bf80000a,
  //   540c380000a,560c280000a,570c280000a,550c380000a,520c580000a,530c580000a,510c680000a,
  //   480ce80000a,4c0cb80000a,4e0ca80000a,4f0ca80000a,4d0cb80000a,4a0cd80000a,4b0cd80000a,
  //   490ce80000a,440d280000a,460d180000a,470d180000a,450d280000a,420d480000a,430d480000a,
  //   410d580000a,200f580000a,300e680000a,380df80000a,3c0dc80000a,3e0db80000a,3f0db80000a,
  //   3d0dc80000a,3a0de80000a,3b0de80000a,390df80000a,340e380000a,360e280000a,370e280000a,
  //   350e380000a,320e580000a,330e580000a,310e680000a,280ee80000a,2c0eb80000a,2e0ea80000a,
  //   2f0ea80000a,2d0eb80000a,2a0ed80000a,2b0ed80000a,290ee80000a,240f280000a,260f180000a,
  //   270f180000a,250f280000a,220f480000a,230f480000a,210f580000a,1010580000a,180fe80000a,
  //   1c0fb80000a,1e0fa80000a,1f0fa80000a,1d0fb80000a,1a0fd80000a,1b0fd80000a,190fe80000a,
  //   1410280000a,1610180000a,1710180000a,1510280000a,1210480000a,1310480000a,1110580000a,
  //   810d80000a,c10a80000a,e10980000a,f10980000a,d10a80000a,a10c80000a,b10c80000a,910d80000a,
  //   411280000a,611080000a,711080000a,511180000a,100036,211580000a,311580000a,80036,111780000a,
  //   117200000,80000880483,3bc,e04bc,100080000c,80484,1600bc,8048b,a00bd,a00be,80484,16348d,
  //   6508c,a00000,10048c,e00be,40000e,c00bb,100830,90088,100830,90089,2043c,1b9,2a00b8,
  //   1b6,1b7,1b0,1b5,1b1,1b2,1b3,1b4,1b8,1b9,1ba,12fc001bb,200000
  //   contents of ROM (hex, n*v repeats v):
  //   75,ff,0,75,fe,0,75,fd,1,75,ff,0,75,fe,0,75,fd,2,75,ff,0,75,fe,0,75,fd,3,75,ff,2,75,
  //   fe,40,75,fd,1,75,ff,2,75,fe,40,75,fd,2,75,ff,2,75,fe,40,75,fd,3,75,ff,de,75,fe,a0,
  //   75,fd,1,75,ff,de,75,fe,a0,75,fd,2,75,ff,de,75,fe,a0,75,fd,3,75,ef,0,75,ee,1
endmodule
